# Fritzing sketch clock_base (saved by Fritzing 0.9.3b)

parts:
  RHT1 = Humidity and Temperature Sensor RHT03
  Part1 = Arduino Uno (Rev3) - ICSP
  R1 = Resistor [tolerance=±5% resistance=4.7k package="2010 [SMD]"]
  R2 = PHOTOCELL [package=photocell-kit]
  R3 = Resistor [tolerance=±5% resistance=10k package="2010 [SMD]"]
  ZS-042_RTC1 = ZS-042 RTC Module
  DI1 = 7-Segment LED Display [package=THT]
  S1 = Round Pushbutton
  S2 = Round Pushbutton
  R4 = Resistor [tolerance=±5% resistance=220 package="0603 [SMD]"]
  R5 = Resistor [tolerance=±5% resistance=220 package="0603 [SMD]"]
  U1 = TCRT5000 [package=THT]
  R7 = Resistor [tolerance=±10% resistance=100 package=THT]
  R6 = Resistor [tolerance=±5% resistance=4.7k package=THT]

nets:
  VCC: RHT1.Vcc, Part1.5V, R1.Pin_0, R2.P$1, ZS-042_RTC1.VCC, DI1.VIN, S1.leg1, S2.leg1, R6.Pin_0
  N1: RHT1.Data-signal, Part1.D13/SCK, R1.Pin_1
  GND: RHT1.GND_2, Part1.GND, R3.Pin_1, ZS-042_RTC1.GND, R4.Pin_1, R5.Pin_1, U1.Pin_2, U1.Pin_3
  N2: Part1.A0, U1.Pin_1, R6.Pin_1
  N3: Part1.A3, R2.P$2, R3.Pin_0
  N4: Part1.ICSP_MISO, Part1.D12/MISO, ZS-042_RTC1.SDA
  N5: Part1.D8, DI1.CLK
  N6: Part1.D9_PWM, DI1.DIO
  N7: Part1.A5/SCL, ZS-042_RTC1.SCL
  N8: Part1.D3_PWM, S2.leg0, R5.Pin_0
  N9: Part1.D4, S1.leg0, R4.Pin_0
  N10: Part1.D6_PWM, R7.Pin_0
  N11: U1.Pin_4, R7.Pin_1

custom parts:
  TCRT5000: TCRT5000 optical reflective sensor
